// Logisim project BellBox(8-bit computer).circ as structural Verilog: 12 circuits, main circuit customcpu 
// Enable
module customcpu (
  input  [7:0] INPUT_BUS,
  input  Enable,
  input  Load,
  input  [7:0] INCANDDEC,
  input  [2:0] in_5,
  input  in_6,
  input  Enable_2,
  input  Load_2,
  input  Enable_3,
  input  Load_3,
  output [7:0] STORED_VALUE,
  output [7:0] ALU_OUTPUT,
  output Z,
  output NF,
  output OF,
  output C,
  output [3:0] Dec,
  output [3:0] ins,
  output [7:0] STORED_VALUE_2
);

  _8bitinstructionregister u_8bitinstructionregister_1 (
    .in_3(INPUT_BUS), .Enable(Enable_2), .Load(Load_2), .for_decoder(Dec), .out_5(ins));
  _8bitregister u_8bitregister_1 (
    .in_1(INPUT_BUS), .Enable(Enable), .Load(Load), ._8BitOutput(STORED_VALUE));  // open: I8, I7, I6, I5, I4, I3, I2, I1
  ALU alu_1 (
    .A(STORED_VALUE), .B(STORED_VALUE_2), .Controlbit(in_5), .zero(Z), .enable(in_6), .negative_flag(NF),
    .overflow_flag(OF), .carry(C), .Output(ALU_OUTPUT), .incanddec(INCANDDEC));
  _8bitregister u_8bitregister_2 (
    .in_1(INPUT_BUS), .Enable(Enable_3), .Load(Load_3), ._8BitOutput(STORED_VALUE_2));  // open: I8, I7, I6, I5, I4, I3, I2, I1

  // Notes on the sheet:
  //   Instruction Register
  //   A
  //   B
endmodule

module FullAdder (
  input  in_1,
  input  in_2,
  input  in_3,
  output Sum,
  output out_5
);

  wire and_1_out, and_2_out, xor_1_out;

  xor xor_1 (xor_1_out, in_1, in_2);
  and and_1 (and_1_out, in_1, in_2);
  xor xor_2 (Sum, xor_1_out, in_3);
  and and_2 (and_2_out, in_3, xor_1_out);
  or or_1 (out_5, and_2_out, and_1_out);
endmodule

module ALU (
  input  [7:0] A,
  input  [7:0] B,
  input  [2:0] Controlbit,
  input  enable,
  input  [7:0] incanddec,
  output zero,
  output [7:0] Output,
  output negative_flag,
  output overflow_flag,
  output carry
);

  wire adder_1_cout, adder_2_cout, subtractor_1_bout, subtractor_2_bout;
  wire [6:0] multiplexer_1_out;
  wire [7:0] adder_1_out, adder_2_out, AND_out, NOT_out, OR_out, subtractor_1_out, subtractor_2_out, XOR_out;

  Adder adder_1 (.a(A), .b(B), .out(adder_1_out), .cout(adder_1_cout));  // open: cin
  Subtractor subtractor_1 (.a(A), .b(B), .out(subtractor_1_out), .bout(subtractor_1_bout));  // open: bin
  assign AND_out = A & B;  // AND_Gate AND, 8 bits wide
  assign OR_out = A | B;  // OR_Gate OR, 8 bits wide
  assign NOT_out = ~A;  // NOT_Gate NOT, 8 bits wide
  Adder adder_2 (.a(A), .b(incanddec), .out(adder_2_out), .cout(adder_2_cout));  // open: cin
  Subtractor subtractor_2 (.a(A), .b(incanddec), .out(subtractor_2_out), .bout(subtractor_2_bout));  // open: bin
  assign XOR_out = A ^ B;  // XOR_Gate XOR, 8 bits wide
  Multiplexer #(.select(3), .width(8), .enable("false")) multiplexer_1 (
    .in0(adder_1_out), .in1(subtractor_1_out), .in2(AND_out), .in3(OR_out), .in4(NOT_out), .in5(adder_2_out),
    .in6(subtractor_2_out), .in7(XOR_out), .out({negative_flag, multiplexer_1_out}), .sel(Controlbit));
  nor nor_1 (zero, multiplexer_1_out[0], multiplexer_1_out[1], multiplexer_1_out[2], multiplexer_1_out[3], multiplexer_1_out[4], multiplexer_1_out[5], multiplexer_1_out[6], negative_flag);
  ExactlyOne xor_2 (.out(overflow_flag), .in0(negative_flag), .in1(B[7]), .in2(A[7]));
  or or_2 (carry, subtractor_1_bout, adder_1_cout, adder_2_cout, subtractor_2_bout);
  assign Output[7] = enable ? negative_flag : 1'bz;  // Controlled_Buffer controlled_buffer_1
  assign Output[2] = enable ? multiplexer_1_out[2] : 1'bz;  // Controlled_Buffer controlled_buffer_2
  assign Output[3] = enable ? multiplexer_1_out[3] : 1'bz;  // Controlled_Buffer controlled_buffer_3
  assign Output[4] = enable ? multiplexer_1_out[4] : 1'bz;  // Controlled_Buffer controlled_buffer_4
  assign Output[5] = enable ? multiplexer_1_out[5] : 1'bz;  // Controlled_Buffer controlled_buffer_5
  assign Output[6] = enable ? multiplexer_1_out[6] : 1'bz;  // Controlled_Buffer controlled_buffer_6
  assign Output[0] = enable ? multiplexer_1_out[0] : 1'bz;  // Controlled_Buffer controlled_buffer_7
  assign Output[1] = enable ? multiplexer_1_out[1] : 1'bz;  // Controlled_Buffer controlled_buffer_8

  // Notes on the sheet:
  //   Incrementer
  //   Decrementor
endmodule

module Adder8bit (
  input  [7:0] A,
  input  Carry_In,
  input  [7:0] B,
  output [7:0] Sum,
  output out_5
);

  wire fulladder_1_out_5, fulladder_2_out_5, fulladder_3_out_5, fulladder_4_out_5, fulladder_5_out_5,
       fulladder_6_out_5, fulladder_7_out_5;

  FullAdder fulladder_1 (.in_1(A[0]), .in_2(B[0]), .in_3(Carry_In), .Sum(Sum[0]), .out_5(fulladder_1_out_5));
  FullAdder fulladder_2 (.in_1(A[1]), .in_2(B[1]), .in_3(fulladder_1_out_5), .Sum(Sum[1]), .out_5(fulladder_2_out_5));
  FullAdder fulladder_3 (.in_1(A[2]), .in_2(B[2]), .in_3(fulladder_2_out_5), .Sum(Sum[2]), .out_5(fulladder_3_out_5));
  FullAdder fulladder_4 (.in_1(A[3]), .in_2(B[3]), .in_3(fulladder_3_out_5), .Sum(Sum[3]), .out_5(fulladder_4_out_5));
  FullAdder fulladder_5 (.in_1(A[4]), .in_2(B[4]), .in_3(fulladder_4_out_5), .Sum(Sum[4]), .out_5(fulladder_5_out_5));
  FullAdder fulladder_6 (.in_1(A[5]), .in_2(B[5]), .in_3(fulladder_5_out_5), .Sum(Sum[5]), .out_5(fulladder_6_out_5));
  FullAdder fulladder_7 (.in_1(A[6]), .in_2(B[6]), .in_3(fulladder_6_out_5), .Sum(Sum[6]), .out_5(fulladder_7_out_5));
  FullAdder fulladder_8 (.in_1(A[7]), .in_2(B[7]), .in_3(fulladder_7_out_5), .Sum(Sum[7]), .out_5(out_5));
endmodule

module Subtractor8bit (
  input  [7:0] A,
  input  [7:0] B,
  output [7:0] Diff
);

  Subtractor subtractor_1 (.a(A), .b(B), .out(Diff));  // open: bin, bout
endmodule

module Final (
  input  load,
  input  clear,
  input  enable,
  input  [7:0] incdec,
  input  [2:0] CB,
  input  E,
  input  load_2,
  input  clear_2,
  input  enable_2,
  output [7:0] Output,
  output [7:0] Output_2,
  output Z,
  output NF,
  output OF,
  output C,
  output [7:0] Output_3
);

  wire clock_1_out;
  wire [7:0] register_1_q, register_2_q;

  DotMatrix #(.matrixcols(8), .matrixrows(1), .dotshape("circle")) dotmatrix_1 (
    .col0(Output[7]), .col1(Output[6]), .col2(Output[5]), .col3(Output[4]), .col4(Output[3]),
    .col5(Output[2]), .col6(Output[1]), .col7(Output[0]));
  Clock clock_1 (.out(clock_1_out));
  ALU alu_1 (
    .A(Output_2), .B(Output_3), .Controlbit(CB), .zero(Z), .enable(E), .negative_flag(NF),
    .overflow_flag(OF), .carry(C), .Output(Output), .incanddec(incdec));
  Register register_1 (.D(Output), .en(load), .Q(register_1_q), .clk(clock_1_out), .clr(clear));
  Register register_2 (.D(Output), .en(load_2), .Q(register_2_q), .clk(clock_1_out), .clr(clear_2));
  assign Output_2[3] = enable ? register_1_q[3] : 1'bz;  // Controlled_Buffer controlled_buffer_1
  assign Output_2[4] = enable ? register_1_q[4] : 1'bz;  // Controlled_Buffer controlled_buffer_2
  assign Output_2[5] = enable ? register_1_q[5] : 1'bz;  // Controlled_Buffer controlled_buffer_3
  assign Output_2[6] = enable ? register_1_q[6] : 1'bz;  // Controlled_Buffer controlled_buffer_4
  assign Output_2[7] = enable ? register_1_q[7] : 1'bz;  // Controlled_Buffer controlled_buffer_5
  assign Output_3[3] = enable_2 ? register_2_q[3] : 1'bz;  // Controlled_Buffer controlled_buffer_6
  assign Output_3[4] = enable_2 ? register_2_q[4] : 1'bz;  // Controlled_Buffer controlled_buffer_7
  assign Output_3[5] = enable_2 ? register_2_q[5] : 1'bz;  // Controlled_Buffer controlled_buffer_8
  assign Output_3[6] = enable_2 ? register_2_q[6] : 1'bz;  // Controlled_Buffer controlled_buffer_9
  assign Output_3[7] = enable_2 ? register_2_q[7] : 1'bz;  // Controlled_Buffer controlled_buffer_10
  assign Output_2[0] = enable ? register_1_q[0] : 1'bz;  // Controlled_Buffer controlled_buffer_11
  assign Output_2[1] = enable ? register_1_q[1] : 1'bz;  // Controlled_Buffer controlled_buffer_12
  assign Output_2[2] = enable ? register_1_q[2] : 1'bz;  // Controlled_Buffer controlled_buffer_13
  assign Output_3[0] = enable_2 ? register_2_q[0] : 1'bz;  // Controlled_Buffer controlled_buffer_14
  assign Output_3[1] = enable_2 ? register_2_q[1] : 1'bz;  // Controlled_Buffer controlled_buffer_15
  assign Output_3[2] = enable_2 ? register_2_q[2] : 1'bz;  // Controlled_Buffer controlled_buffer_16

  // Notes on the sheet:
  //   INPUT BUS
endmodule

module d_flip_flop (
  input  in_1,
  output out_2,
  output out_3
);

  wire clock_1_out, nand_1_out, nand_2_out, not_1_out;

  Clock #(.highDuration(2), .lowDuration(2)) clock_1 (.out(clock_1_out));
  not not_1 (not_1_out, in_1);
  nand nand_1 (nand_1_out, in_1, clock_1_out);
  nand nand_2 (nand_2_out, not_1_out, clock_1_out);
  nand nand_3 (out_2, nand_1_out, out_3);
  nand nand_4 (out_3, out_2, nand_2_out);
endmodule

module _1bitregister (
  input  load,
  input  data,
  input  enable,
  output out_4,
  output out_5
);

  wire and_1_out, and_2_out, d_flip_flop_1_out_2, not_1_out, or_1_out;

  not not_1 (not_1_out, load);
  and and_1 (and_1_out, d_flip_flop_1_out_2, not_1_out);
  and and_2 (and_2_out, load, data);
  or or_1 (or_1_out, and_1_out, and_2_out);
  d_flip_flop d_flip_flop_1 (.in_1(or_1_out), .out_2(d_flip_flop_1_out_2), .out_3(out_5));
  and and_3 (out_4, d_flip_flop_1_out_2, enable);

  // Notes on the sheet:
  //   D-flip flop
  //   Trisate Buffer
endmodule

// Register
module _8bitregister (
  input  [7:0] in_1,
  input  Enable,
  input  Load,
  output I8,
  output I7,
  output I6,
  output [7:0] _8BitOutput,
  output I5,
  output I4,
  output I3,
  output I2,
  output I1
);

  _1bitregister u_1bitregister_1 (.load(Load), .data(in_1[7]), .enable(Enable), .out_4(_8BitOutput[7]));  // open: out_5
  _1bitregister u_1bitregister_2 (.load(Load), .data(in_1[6]), .enable(Enable), .out_4(_8BitOutput[6]));  // open: out_5
  _1bitregister u_1bitregister_3 (.load(Load), .data(in_1[5]), .enable(Enable), .out_4(_8BitOutput[5]));  // open: out_5
  _1bitregister u_1bitregister_4 (.load(Load), .data(in_1[4]), .enable(Enable), .out_4(_8BitOutput[4]));  // open: out_5
  _1bitregister u_1bitregister_5 (.load(Load), .data(in_1[3]), .enable(Enable), .out_4(_8BitOutput[3]));  // open: out_5
  _1bitregister u_1bitregister_6 (.load(Load), .data(in_1[2]), .enable(Enable), .out_4(_8BitOutput[2]));  // open: out_5
  _1bitregister u_1bitregister_7 (.load(Load), .data(in_1[1]), .enable(Enable), .out_4(_8BitOutput[1]));  // open: out_5
  _1bitregister u_1bitregister_8 (.load(Load), .data(in_1[0]), .enable(Enable), .out_4(_8BitOutput[0]));  // open: out_5

  assign I1 = _8BitOutput[0];
  assign I2 = _8BitOutput[1];
  assign I3 = _8BitOutput[2];
  assign I4 = _8BitOutput[3];
  assign I5 = _8BitOutput[4];
  assign I6 = _8BitOutput[5];
  assign I7 = _8BitOutput[6];
  assign I8 = _8BitOutput[7];
endmodule

module _8bitinstructionregister (
  input  Enable,
  input  Load,
  input  [7:0] in_3,
  output [3:0] for_decoder,
  output [3:0] out_5
);

  _8bitregister u_8bitregister_1 (
    .in_1(in_3), .Enable(Enable), .Load(Load), .I8(for_decoder[3]), .I7(for_decoder[2]), .I6(for_decoder[1]),
    .I5(for_decoder[0]), .I4(out_5[3]), .I3(out_5[2]), .I2(out_5[1]), .I1(out_5[0]));  // open: _8BitOutput
endmodule

module semi8bitregister (
  input  [7:0] \input ,
  input  load,
  input  clear,
  input  enable,
  output [7:0] Output
);

  wire clock_1_out;
  wire [7:0] register_1_q;

  Register register_1 (.D(\input ), .en(load), .Q(register_1_q), .clk(clock_1_out), .clr(clear));
  Clock clock_1 (.out(clock_1_out));
  assign Output[6] = enable ? register_1_q[6] : 1'bz;  // Controlled_Buffer controlled_buffer_1
  assign Output[7] = enable ? register_1_q[7] : 1'bz;  // Controlled_Buffer controlled_buffer_2
  assign Output[1] = enable ? register_1_q[1] : 1'bz;  // Controlled_Buffer controlled_buffer_3
  assign Output[2] = enable ? register_1_q[2] : 1'bz;  // Controlled_Buffer controlled_buffer_4
  assign Output[3] = enable ? register_1_q[3] : 1'bz;  // Controlled_Buffer controlled_buffer_5
  assign Output[4] = enable ? register_1_q[4] : 1'bz;  // Controlled_Buffer controlled_buffer_6
  assign Output[5] = enable ? register_1_q[5] : 1'bz;  // Controlled_Buffer controlled_buffer_7
  assign Output[0] = enable ? register_1_q[0] : 1'bz;  // Controlled_Buffer controlled_buffer_8
endmodule

module rammodule (
  input  addregisterenble,
  input  [3:0] addressinputregister,
  input  [3:0] addressinputdirect,
  input  addressmuxenable,
  input  storevalueintotheram,
  input  loadvaluetooutput,
  input  dataregisterenable,
  input  [7:0] datainputregister,
  input  datamuxenable,
  input  [7:0] datainputdirect,
  output [3:0] addregisterputput,
  output [7:0] OutputofRam,
  output [7:0] dataregisteroutput
);

  wire clear_out, clock_out;
  wire [3:0] register_1_q;
  wire [7:0] register_2_q;

  Clock clock (.out(clock_out));
  Register #(.width(4)) register_1 (
    .D(addressinputregister), .en(addregisterenble), .Q(register_1_q), .clk(clock_out));  // open: clr
  Button clear (.out(clear_out));
  Multiplexer #(.width(4)) multiplexer_1 (
    .in0(register_1_q), .in1(addressinputdirect), .out(addregisterputput), .sel(addressmuxenable));  // open: en
  Register register_2 (.D(datainputregister), .en(dataregisterenable), .Q(register_2_q), .clk(clock_out));  // open: clr
  Multiplexer #(.width(8)) multiplexer_2 (
    .in0(register_2_q), .in1(datainputdirect), .out(dataregisteroutput), .sel(datamuxenable));  // open: en
  RAM #(.addrWidth(4), .bus("separate")) ram_1 (
    .addr(addregisterputput), .din(dataregisteroutput), .data(OutputofRam), .str(storevalueintotheram),
    .sel(1'b1), .clk(clock_out), .ld(loadvaluetooutput), .clr(clear_out));
  RAM #(.addrWidth(4), .bus("separate")) ram_2 (
    .addr(addregisterputput), .din(dataregisteroutput), .data(OutputofRam), .str(storevalueintotheram),
    .sel(1'b1), .clk(clock_out), .ld(loadvaluetooutput), .clr(clear_out));
endmodule
